# Fritzing sketch Light Dimmer (saved by Fritzing 1.0.4)
perfboards: 2

parts:
  WeMos_D1_Mini1 = WeMos D1 Mini
  Part1 = IFR520 MOS module [package=THT]
  LED1 = smd LED [color="White (4500K)" package="1206 [SMD]"]
  U1 = ENCODER_RGB_CA [package=encoder_led_3]
  U2 = Mini-360 DC-DC Buck converter [package=THT]
  PIR1 = PIR sensor
  J1 = Camdenboss CTB0158-2 [part_number=CTB0158-2 package=THT]
  WeMos_D1_Mini2 = WeMos D1 Mini  # not connected
  J2 = female pin header, 5 pins [form="♀ (female)"]  # not connected
  J3 = female pin header, 3 pins [form="♀ (female)"]  # not connected
  U3 = Mini-360 DC-DC Buck converter [package=THT]  # not connected
  J4 = female pin header, 3 pins [form="♀ (female)"]
  J5 = female pin header, 5 pins [form="♀ (female)"]
  J6 = female pin header, 4 pins [form="♀ (female)"]
  J7 = female pin header, 6 pins [form="♀ (female)"]
  J8 = female pin header, 6 pins [form="♀ (female)"]  # not connected
  J9 = female pin header, 8 pins [form="♀ (female)"]
  J10 = female pin header, 8 pins [form="♀ (female)"]

nets:
  5V: WeMos_D1_Mini1.5V, Part1.VCC, U1.B, U2.OUT-, PIR1.VDD
  N1: WeMos_D1_Mini1.D1, U1.-B
  N2: WeMos_D1_Mini1.D2, U1.+
  N3: WeMos_D1_Mini1.D3, U1.A
  N4: WeMos_D1_Mini1.D5, PIR1.SIG
  N5: WeMos_D1_Mini1.D8, Part1.SIG
  GND: WeMos_D1_Mini1.G, Part1.GND, U1.C, U2.IN-, U2.OUT+, PIR1.GND, J1.terminal_1
  N6: Part1.V+, LED1.cathode
  N7: Part1.V-, LED1.anode
  N8: Part1.VIN, U2.IN+, J1.terminal_2
  N9: J4.pin1, J5.pin2, J7.pin1, J9.pin1
  N10: J4.pin2, J10.pin5
  N11: J4.pin3, J5.pin1, J6.pin3, J7.pin6, J9.pin2
  N12: J5.pin3, J9.pin4
  N13: J5.pin4, J9.pin5
  N14: J5.pin5, J9.pin6
  N15: J6.pin2, J10.pin2

notes:
  12V In
  12V Out
  CLK DT SW + GND
  GND + SW DT CLK
  + o -
  12V

custom parts:
  Mini-360 DC-DC Buck converter: Mini-360 DC-DC Buck converter. Tiny buck step down voltage converter, input voltage 4.75 to 23V output 1 to 17V adjustable. Available from ebay and the like.
